// Logisim project control-logic.circ as structural Verilog: 1 circuit, main circuit control_logic
module control_logic (
  input  [31:0] inst,
  input  BrEq,
  input  BrLt,
  output PCSel,
  output RegWEn,
  output [2:0] ImmSel,
  output BrUn,
  output ASel,
  output BSel,
  output [3:0] ALUSel,
  output MemRW,
  output [1:0] WBSel,
  output CSRSel,
  output CSRWen
);

  wire and_1_out, and_2_out, and_3_out, and_4_out, and_5_out, and_6_out, and_7_out, and_8_out, and_9_out,
       and_10_out, and_11_out, and_12_out, and_13_out, and_14_out, and_15_out, and_16_out, and_17_out,
       and_18_out, and_19_out, and_20_out, and_21_out, and_22_out, and_23_out, and_24_out, and_25_out,
       and_26_out, and_27_out, and_28_out, and_29_out, and_30_out, and_31_out, and_32_out, and_33_out,
       and_34_out, and_35_out, and_36_out, and_37_out, and_38_out, funct3_0b000, funct3_0b001, funct3_0b010,
       funct3_0b011, funct3_0b100, funct3_0b101, funct3_0b110, funct3_0b111, funct7_0b0000000,
       funct7_0b0000001, funct7_0b0100000, not_1_out, not_2_out, not_3_out, not_5_out, not_6_out,
       opcode_0b0000011, opcode_0b0010011, opcode_0b0010111, opcode_0b0100011, opcode_0b0110011,
       opcode_0b0110111, opcode_0b1100011, opcode_0b1100111, opcode_0b1101111, opcode_0b1110011, or_2_out,
       priority_encoder_5_out, priority_encoder_8_out, xor_1_out, xor_2_out;
  wire [1:0] priority_encoder_1_out, priority_encoder_4_out, priority_encoder_6_out;
  wire [2:0] priority_encoder_2_out, priority_encoder_7_out;
  wire [3:0] priority_encoder_3_out;
  wire [5:0] bit_extender_1_out, bit_extender_2_out, bit_extender_3_out, bit_extender_4_out,
       bit_extender_5_out, bit_extender_6_out, bit_extender_7_out, bit_extender_8_out, ROM_input;

  Comparator #(.mode("unsigned"), .width(7)) comparator_1 (
    .a(inst[6:0]), .b(7'b0110011), .eq(opcode_0b0110011));  // open: gt, lt
  Comparator #(.mode("unsigned"), .width(7)) comparator_2 (
    .a(inst[6:0]), .b(7'b0000011), .eq(opcode_0b0000011));  // open: gt, lt
  Comparator #(.mode("unsigned"), .width(7)) comparator_3 (
    .a(inst[6:0]), .b(7'b0010011), .eq(opcode_0b0010011));  // open: gt, lt
  Comparator #(.mode("unsigned"), .width(7)) comparator_4 (
    .a(inst[6:0]), .b(7'b0100011), .eq(opcode_0b0100011));  // open: gt, lt
  Comparator #(.mode("unsigned"), .width(7)) comparator_5 (
    .a(inst[6:0]), .b(7'b1100011), .eq(opcode_0b1100011));  // open: gt, lt
  Comparator #(.mode("unsigned"), .width(7)) comparator_6 (
    .a(inst[6:0]), .b(7'b0010111), .eq(opcode_0b0010111));  // open: gt, lt
  Comparator #(.mode("unsigned"), .width(7)) comparator_7 (
    .a(inst[6:0]), .b(7'b0110111), .eq(opcode_0b0110111));  // open: gt, lt
  Comparator #(.mode("unsigned"), .width(7)) comparator_8 (
    .a(inst[6:0]), .b(7'b1101111), .eq(opcode_0b1101111));  // open: gt, lt
  Comparator #(.mode("unsigned"), .width(7)) comparator_9 (
    .a(inst[6:0]), .b(7'b1100111), .eq(opcode_0b1100111));  // open: gt, lt
  Comparator #(.mode("unsigned"), .width(7)) comparator_10 (
    .a(inst[6:0]), .b(7'b1110011), .eq(opcode_0b1110011));  // open: gt, lt
  ROM #(.addrWidth(6), .dataWidth(16)) rom_1 (
    .addr(ROM_input), .data({RegWEn, ImmSel, BrUn, ASel, BSel, ALUSel, MemRW, WBSel, CSRSel, CSRWen}));
  and and_1 (and_1_out, funct3_0b000, opcode_0b0100011);
  and and_2 (and_2_out, funct3_0b001, opcode_0b0100011);
  and and_3 (and_3_out, funct3_0b010, opcode_0b0100011);
  and and_4 (and_4_out, funct3_0b000, opcode_0b1100011);
  and and_5 (and_5_out, funct3_0b001, opcode_0b1100011);
  and and_6 (and_6_out, funct3_0b100, opcode_0b1100011);
  and and_7 (and_7_out, funct3_0b101, opcode_0b1100011);
  and and_8 (and_8_out, funct3_0b110, opcode_0b1100011);
  and and_9 (and_9_out, funct3_0b111, opcode_0b1100011);
  and and_10 (and_10_out, funct3_0b000, funct7_0b0000000, opcode_0b0110011);
  and and_11 (and_11_out, funct3_0b000, funct7_0b0000001, opcode_0b0110011);
  and and_12 (and_12_out, funct3_0b000, funct7_0b0100000, opcode_0b0110011);
  and and_13 (and_13_out, funct3_0b001, funct7_0b0000000, opcode_0b0110011);
  and and_14 (and_14_out, funct3_0b001, funct7_0b0000001, opcode_0b0110011);
  and and_15 (and_15_out, funct3_0b011, funct7_0b0000001, opcode_0b0110011);
  and and_16 (and_16_out, funct3_0b010, funct7_0b0000000, opcode_0b0110011);
  and and_17 (and_17_out, funct3_0b100, funct7_0b0000000, opcode_0b0110011);
  and and_18 (and_18_out, funct3_0b101, funct7_0b0000000, opcode_0b0110011);
  and and_19 (and_19_out, funct3_0b101, funct7_0b0100000, opcode_0b0110011);
  and and_20 (and_20_out, funct3_0b110, funct7_0b0000000, opcode_0b0110011);
  and and_21 (and_21_out, funct3_0b111, funct7_0b0000000, opcode_0b0110011);
  Priority_Encoder #(.select(2)) priority_encoder_1 (
    .in0(and_1_out), .in1(and_2_out), .in2(and_3_out), .out(priority_encoder_1_out));  // open: in3, gs, en_out, en_in
  Priority_Encoder priority_encoder_2 (
    .in0(and_4_out), .in1(and_5_out), .in2(and_6_out), .in3(and_7_out), .in4(and_8_out), .in5(and_9_out),
    .out(priority_encoder_2_out));  // open: in6, in7, en_in, gs, en_out
  Comparator #(.mode("unsigned"), .width(3)) comparator_11 (
    .a(inst[14:12]), .b(3'b000), .eq(funct3_0b000));  // open: gt, lt
  Comparator #(.mode("unsigned"), .width(3)) comparator_12 (
    .a(inst[14:12]), .b(3'b001), .eq(funct3_0b001));  // open: gt, lt
  Comparator #(.mode("unsigned"), .width(3)) comparator_13 (
    .a(inst[14:12]), .b(3'b010), .eq(funct3_0b010));  // open: gt, lt
  Comparator #(.mode("unsigned"), .width(3)) comparator_14 (
    .a(inst[14:12]), .b(3'b011), .eq(funct3_0b011));  // open: gt, lt
  Comparator #(.mode("unsigned"), .width(3)) comparator_15 (
    .a(inst[14:12]), .b(3'b100), .eq(funct3_0b100));  // open: gt, lt
  Comparator #(.mode("unsigned"), .width(3)) comparator_16 (
    .a(inst[14:12]), .b(3'b101), .eq(funct3_0b101));  // open: gt, lt
  Comparator #(.mode("unsigned"), .width(3)) comparator_17 (
    .a(inst[14:12]), .b(3'b110), .eq(funct3_0b110));  // open: gt, lt
  Comparator #(.mode("unsigned"), .width(3)) comparator_18 (
    .a(inst[14:12]), .b(3'b111), .eq(funct3_0b111));  // open: gt, lt
  assign bit_extender_1_out = {{4{1'b0}}, priority_encoder_1_out};  // Bit_Extender bit_extender_1
  assign bit_extender_2_out = {{3{1'b0}}, priority_encoder_2_out};  // Bit_Extender bit_extender_2
  Priority_Encoder #(.select(4)) priority_encoder_3 (
    .in0(and_10_out), .in1(and_11_out), .in2(and_12_out), .in3(and_13_out), .in4(and_14_out),
    .in5(and_15_out), .in6(and_16_out), .in7(and_17_out), .in8(and_18_out), .in9(and_19_out),
    .in10(and_20_out), .in11(and_21_out), .out(priority_encoder_3_out));  // open: in12, in13, in14, in15, gs, en_out, en_in
  Adder #(.width(6)) adder_1 (.a(bit_extender_1_out), .b(6'b010111), .out(ROM_input));  // open: cin, cout
  Adder #(.width(6)) adder_2 (.a(bit_extender_2_out), .b(6'b011010), .out(ROM_input));  // open: cin, cout
  or or_1 (PCSel, and_22_out, opcode_0b1101111, opcode_0b1100111);
  assign bit_extender_3_out = {{2{1'b0}}, priority_encoder_3_out};  // Bit_Extender bit_extender_3
  Adder #(.width(6)) adder_3 (.a(bit_extender_3_out), .b({6{1'b0}}), .out(ROM_input));  // open: cin, cout
  and and_22 (and_22_out, inst[0], inst[1], not_1_out, not_2_out, not_3_out, inst[5], inst[6], or_2_out);
  Comparator #(.mode("unsigned"), .width(7)) comparator_19 (
    .a(inst[31:25]), .b({7{1'b0}}), .eq(funct7_0b0000000));  // open: gt, lt
  Comparator #(.mode("unsigned"), .width(7)) comparator_20 (
    .a(inst[31:25]), .b(7'b0000001), .eq(funct7_0b0000001));  // open: gt, lt
  Comparator #(.mode("unsigned"), .width(7)) comparator_21 (
    .a(inst[31:25]), .b(7'b0100000), .eq(funct7_0b0100000));  // open: gt, lt
  not not_1 (not_1_out, inst[2]);
  not not_2 (not_2_out, inst[3]);
  not not_3 (not_3_out, inst[4]);
  Priority_Encoder #(.select(2)) priority_encoder_4 (
    .in0(opcode_0b0010111), .in1(opcode_0b0110111), .in2(opcode_0b1101111), .out(priority_encoder_4_out));  // open: in3, gs, en_out, en_in
  or or_2 (or_2_out, and_23_out, and_24_out);
  assign bit_extender_4_out = {{4{1'b0}}, priority_encoder_4_out};  // Bit_Extender bit_extender_4
  and and_23 (and_23_out, not_5_out, not_6_out, xor_2_out);
  and and_24 (and_24_out, inst[14], xor_1_out);
  Adder #(.width(6)) adder_4 (.a(bit_extender_4_out), .b(6'b100000), .out(ROM_input));  // open: cin, cout
  and and_25 (and_25_out, funct3_0b001, opcode_0b1110011);
  and and_26 (and_26_out, funct3_0b101, opcode_0b1110011);
  Priority_Encoder #(.select(1)) priority_encoder_5 (
    .in0(and_25_out), .in1(and_26_out), .out(priority_encoder_5_out));  // open: gs, en_out, en_in
  xor xor_1 (xor_1_out, inst[12], BrLt);
  assign bit_extender_5_out = {{5{1'b0}}, priority_encoder_5_out};  // Bit_Extender bit_extender_5
  xor xor_2 (xor_2_out, inst[12], BrEq);
  and and_27 (and_27_out, funct3_0b000, opcode_0b0000011);
  and and_28 (and_28_out, funct3_0b001, opcode_0b0000011);
  and and_29 (and_29_out, funct3_0b010, opcode_0b0000011);
  // NOT_Gate not_4 has open pins: in=inst[12], out=open
  not not_5 (not_5_out, inst[13]);
  not not_6 (not_6_out, inst[14]);
  Adder #(.width(6)) adder_5 (.a(bit_extender_5_out), .b(6'b100100), .out(ROM_input));  // open: cin, cout
  Priority_Encoder #(.select(2)) priority_encoder_6 (
    .in0(and_27_out), .in1(and_28_out), .in2(and_29_out), .out(priority_encoder_6_out));  // open: in3, gs, en_out, en_in
  and and_30 (and_30_out, funct3_0b000, opcode_0b0010011);
  and and_31 (and_31_out, funct3_0b001, funct7_0b0000000, opcode_0b0010011);
  and and_32 (and_32_out, funct3_0b010, opcode_0b0010011);
  and and_33 (and_33_out, funct3_0b100, opcode_0b0010011);
  and and_34 (and_34_out, funct3_0b101, funct7_0b0000000, opcode_0b0010011);
  and and_35 (and_35_out, funct3_0b101, funct7_0b0100000, opcode_0b0010011);
  and and_36 (and_36_out, funct3_0b110, opcode_0b0010011);
  and and_37 (and_37_out, funct3_0b111, opcode_0b0010011);
  assign bit_extender_6_out = {{4{1'b0}}, priority_encoder_6_out};  // Bit_Extender bit_extender_6
  Adder #(.width(6)) adder_6 (.a(bit_extender_6_out), .b(6'b001100), .out(ROM_input));  // open: cin, cout
  Priority_Encoder priority_encoder_7 (
    .in0(and_30_out), .in1(and_31_out), .in2(and_32_out), .in3(and_33_out), .in4(and_34_out),
    .in5(and_35_out), .in6(and_36_out), .in7(and_37_out), .out(priority_encoder_7_out));  // open: en_in, gs, en_out
  and and_38 (and_38_out, opcode_0b1100111, funct3_0b000);
  Priority_Encoder #(.select(1)) priority_encoder_8 (
    .in0(and_38_out), .out(priority_encoder_8_out));  // open: in1, gs, en_out, en_in
  assign bit_extender_7_out = {{3{1'b0}}, priority_encoder_7_out};  // Bit_Extender bit_extender_7
  assign bit_extender_8_out = {{5{1'b0}}, priority_encoder_8_out};  // Bit_Extender bit_extender_8
  Adder #(.width(6)) adder_7 (.a(bit_extender_7_out), .b(6'b001111), .out(ROM_input));  // open: cin, cout
  Adder #(.width(6)) adder_8 (.a(bit_extender_8_out), .b(6'b100011), .out(ROM_input));  // open: cin, cout

  // Other names for the same wires on the sheet: opcode[6:0] = inst[6:0]; funct3[2:0] = inst[14:12];
  //   funct7[6:0] = inst[31:25]

  // Notes on the sheet:
  //   INPUTS to your circuit
  //   contents of rom_1 (hex, n*v repeats v):
  //   8004 8104 8184 8024 8124 8164 8044 8084 80a4 81a4 80c4 80e4 9200 9200 9200 9204 9224 9244 9284 92a4
  //   93a4 92c4 92e4 2210 2210 2210 4*3600 3e00 3e00 c604 c3e4 d608 9208 8205 e207
  //   ROM FOR CONTROL LOGIC
  //   R-type
  //   I-type(load)
  //   I-type
  //   S-type
  //   SB-type
  //   U-type(auipc)
  //   U-type(lui)
  //   UJ-type
  //   I-type(jalr)
  //   CSR
  //   DON'T CHANGE THE LOCATIONS OF THE INPUTS AND OUTPUTS!
  //   OUTPUT from your circuit
  //   S-type
  //   SB-type
  //   R-type
  //   U-type, J-type
  //   CSR
  //   load
  //   I-type
  //   jalr
endmodule
